# Fritzing sketch fan-speed-controller (saved by Fritzing 0.9.3b)
circuit board: 4cm x 4.5cm
stripboards: 1

parts:
  7805 = Voltage Regulator [package=to220-igo]
  10kΩ = Resistor [tolerance=±5% resistance=10k power=0.25 package=THT]
  1kΩ = Resistor [tolerance=±5% resistance=1k power=0.25 package=THT]
  100nf = Ceramic Capacitor [capacitance=100nF voltage=35V package="100 mil [THT, multilayer]"]
  330nf = Ceramic Capacitor [capacitance=0pF voltage=35V package="100 mil [THT, multilayer]"]
  20kΩ = Resistor [tolerance=±5% resistance=22k power=0.25 package=THT]
  ATTINY85 = attiny85 [package=dip]
  STA509A_MOSFET_Array = mystery part, 10 pins [chip_label=?]
  IFR4095 = Basic FET P-Channel [part_number=IFR4092 package="TO220 [THT]"]
  2_2Ω = Resistor [tolerance=±5% resistance=1k power=0.25 package=THT]
  PC817 = TLP621 [part_number=PC817 package=THT]
  Terminal_Block = screw terminal, 7 pins
  47nf = Ceramic Capacitor [capacitance=100nF voltage=35V package="200 mil [THT, multilayer]"]

nets:
  N1: 7805.GND, 100nf.1, 330nf.0, 20kΩ.Pin_1, ATTINY85.Pin_4, STA509A_MOSFET_Array.pin1, STA509A_MOSFET_Array.pin10, PC817.Pin_2, PC817.Pin_3, Terminal_Block.pin6, 47nf.1
  N2: 7805.IN, 1kΩ.Pin_0, 330nf.1, IFR4095.source, Terminal_Block.pin1
  N3: 7805.OUT, 10kΩ.Pin_1, 100nf.0, ATTINY85.Pin_8
  N4: 10kΩ.Pin_0, ATTINY85.Pin_1
  N5: 1kΩ.Pin_1, IFR4095.gate, PC817.Pin_4
  N6: 20kΩ.Pin_0, ATTINY85.Pin_3, PC817.Pin_1
  N7: ATTINY85.Pin_2, STA509A_MOSFET_Array.pin9
  N8: ATTINY85.Pin_5, STA509A_MOSFET_Array.pin7
  N9: ATTINY85.Pin_6, STA509A_MOSFET_Array.pin5
  N10: ATTINY85.Pin_7, STA509A_MOSFET_Array.pin3
  N11: STA509A_MOSFET_Array.pin2, Terminal_Block.pin2
  N12: STA509A_MOSFET_Array.pin4, Terminal_Block.pin3
  N13: STA509A_MOSFET_Array.pin6, Terminal_Block.pin4
  N14: STA509A_MOSFET_Array.pin8, Terminal_Block.pin5
  N15: IFR4095.drain, 2_2Ω.Pin_1
  N16: 2_2Ω.Pin_0, Terminal_Block.pin7, 47nf.0

notes:
  12V
  GND
  OUT
  SW1
  SW2
  SW3
  SW4
  Fan Speed Controller v7.0
  ©2022 That Ain't Working
